# Fritzing sketch Schematic (saved by Fritzing 0.9.3b)

parts:
  Часть1 = Arduino Nano (Rev3.0) (ICSP)
  R1 = Resistor [tolerance=±5% resistance=10k package=THT]
  R2 = Resistor [tolerance=±5% resistance=100 package=THT]
  Grove1 = Grove OLED 128x96
  S1 = Pushbutton [package="[THT]"]
  S2 = Pushbutton [package="[THT]"]
  S3 = Pushbutton [package="[THT]"]
  L1 = Inductor [package="400 mil [THT]"]
  S4 = Round Pushbutton
  Часть2 = DC-DC Power Module (5v)
  S5 = Toggle Switch [package=THT]
  18650_holder2 = 18650 holder [package="DIP (Dual Inline) [THT]"]
  18650_holder3 = 18650 holder [package="DIP (Dual Inline) [THT]"]
  Q1 = Basic FET P-Channel [package="D2Pak [SMD]"]

nets:
  GND: Часть1.GND, Grove1.GND, S2.Pin_2, S3.Pin_4, S4.leg1, Часть2.GND*
  N1: Часть1.D2, S4.leg0
  N2: Часть1.D3, S1.Pin_1, S1.Pin_2
  N3: Часть1.D4, S3.Pin_1, S3.Pin_2
  N4: Часть1.D5, S2.Pin_3, S2.Pin_4
  N5: Часть1.D10, R2.Pin_0
  5V: Часть1.5V, Grove1.VCC, Часть2.Vout
  N6: Часть1.A5, Grove1.SDA
  N7: Часть1.A4, Grove1.SCL
  N8: Часть1.A2, Часть2.Vin, S5.COM
  N9: R1.Pin_0, R2.Pin_1, Q1.Gate
  N10: R1.Pin_1, Часть2.GND, 18650_holder2.holder_-, 18650_holder3.holder_-, Q1.source
  N11: L1.pin_0, Q1.drain
  N12: L1.pin_1, S5.L2, 18650_holder2.holder_+, 18650_holder3.holder_+

custom parts:
  DC-DC Power Module (5v): DC-DC Power Module based con AMS1117-5.0 Input: DC 6~12V (input power must higher 1V than output power); Output: 5V (+/-0.05V error), 800mA
  18650 holder: Акум формата 18650 в холдере
